// Logisim project SP18-CSE231-1.circ as structural Verilog: 8 circuits, main circuit main
module main (
  input  D,
  input  C,
  input  B,
  input  A
);

  wire n4_16_decoder_1_out_6, n4_16_decoder_1_out_7, n4_16_decoder_1_out_8, n4_16_decoder_1_out_9,
       n4_16_decoder_1_out_10, n4_16_decoder_1_out_11, n4_16_decoder_1_out_12, n4_16_decoder_1_out_13,
       n4_16_decoder_1_out_14, n4_16_decoder_1_out_15, n4_16_decoder_1_out_16, n4_16_decoder_1_out_17,
       n4_16_decoder_1_out_18, or_1_out, or_2_out, or_3_out, or_4_out, or_5_out, or_6_out, or_7_out;

  _4_16_decoder u_4_16_decoder_1 (
    .out_6(n4_16_decoder_1_out_6), .out_7(n4_16_decoder_1_out_7), .out_8(n4_16_decoder_1_out_8),
    .out_9(n4_16_decoder_1_out_9), .out_10(n4_16_decoder_1_out_10), .out_11(n4_16_decoder_1_out_11),
    .out_12(n4_16_decoder_1_out_12), .out_13(n4_16_decoder_1_out_13), .out_14(n4_16_decoder_1_out_14),
    .out_15(n4_16_decoder_1_out_15), .out_16(n4_16_decoder_1_out_16), .out_17(n4_16_decoder_1_out_17),
    .out_18(n4_16_decoder_1_out_18), .in_1(A), .in_2(B), .in_3(C), .in_4(D));  // open: out_5, out_19, out_20
  or or_1 (or_1_out, n4_16_decoder_1_out_6, n4_16_decoder_1_out_7, n4_16_decoder_1_out_9, n4_16_decoder_1_out_11, n4_16_decoder_1_out_12, n4_16_decoder_1_out_13, n4_16_decoder_1_out_14, n4_16_decoder_1_out_15);
  or or_2 (or_2_out, n4_16_decoder_1_out_7, n4_16_decoder_1_out_8, n4_16_decoder_1_out_9, n4_16_decoder_1_out_14, n4_16_decoder_1_out_15, n4_16_decoder_1_out_16, n4_16_decoder_1_out_18);
  or or_3 (or_3_out, n4_16_decoder_1_out_6, n4_16_decoder_1_out_8, n4_16_decoder_1_out_9, n4_16_decoder_1_out_12, n4_16_decoder_1_out_15, n4_16_decoder_1_out_16, n4_16_decoder_1_out_18);
  or or_4 (or_4_out, n4_16_decoder_1_out_6, n4_16_decoder_1_out_9, n4_16_decoder_1_out_11, n4_16_decoder_1_out_12, n4_16_decoder_1_out_13, n4_16_decoder_1_out_14, n4_16_decoder_1_out_15);
  or or_5 (or_5_out, n4_16_decoder_1_out_7, n4_16_decoder_1_out_9, n4_16_decoder_1_out_11, n4_16_decoder_1_out_13, n4_16_decoder_1_out_14);
  or or_6 (or_6_out, n4_16_decoder_1_out_6, n4_16_decoder_1_out_7, n4_16_decoder_1_out_9, n4_16_decoder_1_out_11, n4_16_decoder_1_out_12, n4_16_decoder_1_out_13);
  or or_7 (or_7_out, n4_16_decoder_1_out_6, n4_16_decoder_1_out_7, n4_16_decoder_1_out_9, n4_16_decoder_1_out_10, n4_16_decoder_1_out_12, n4_16_decoder_1_out_13, n4_16_decoder_1_out_14, n4_16_decoder_1_out_15, n4_16_decoder_1_out_17);
  _7_Segment_Display u_7_segment_display_1 (
    .g(or_7_out), .f(or_6_out), .a(or_1_out), .b(or_2_out), .e(or_5_out), .d(or_4_out), .c(or_3_out));  // open: dp
endmodule

module _4_16_decoder (
  input  in_1,
  input  in_2,
  input  in_3,
  input  in_4,
  output out_5,
  output out_6,
  output out_7,
  output out_8,
  output out_9,
  output out_10,
  output out_11,
  output out_12,
  output out_13,
  output out_14,
  output out_15,
  output out_16,
  output out_17,
  output out_18,
  output out_19,
  output out_20
);

  wire not_1_out, not_2_out, not_3_out, not_4_out;

  not not_1 (not_1_out, in_1);
  not not_2 (not_2_out, in_2);
  not not_3 (not_3_out, in_4);
  not not_4 (not_4_out, in_3);
  and and_1 (out_5, not_1_out, not_2_out, not_4_out, not_3_out);
  and and_2 (out_6, not_1_out, not_2_out, not_4_out, in_4);
  and and_3 (out_7, not_1_out, not_2_out, in_3, not_3_out);
  and and_4 (out_8, not_1_out, not_2_out, in_3, in_4);
  and and_5 (out_9, not_1_out, in_2, not_4_out, not_3_out);
  and and_6 (out_10, not_1_out, in_2, not_4_out, in_4);
  and and_7 (out_11, not_1_out, in_2, in_3, not_3_out);
  and and_8 (out_12, not_1_out, in_2, in_3, in_4);
  and and_9 (out_13, in_1, not_2_out, not_4_out, not_3_out);
  and and_10 (out_14, in_1, not_2_out, not_4_out, in_4);
  and and_11 (out_15, in_1, not_2_out, in_3, not_3_out);
  and and_12 (out_16, in_1, not_2_out, in_3, in_4);
  and and_13 (out_17, in_1, in_2, not_4_out, not_3_out);
  and and_14 (out_18, in_1, in_2, not_4_out, in_4);
  and and_15 (out_19, in_1, in_2, in_3, not_3_out);
  and and_16 (out_20, in_1, in_2, in_3, in_4);
endmodule

module Basic_Gate (
  input  A,
  input  B,
  input  C,
  input  D
);

  wire and_1_out, and_2_out, and_3_out, and_4_out, and_5_out, and_6_out, and_7_out, and_8_out, and_9_out,
       and_10_out, and_11_out, and_12_out, and_13_out, and_14_out, and_15_out, and_16_out, and_17_out,
       and_18_out, and_19_out, and_20_out, and_21_out, and_22_out, and_23_out, and_24_out, and_25_out,
       and_26_out, and_27_out, and_28_out, and_29_out, and_30_out, not_1_out, not_2_out, not_3_out,
       not_4_out, or_1_out, or_2_out, or_3_out, or_4_out, or_5_out, or_6_out, or_7_out;

  not not_1 (not_1_out, A);
  not not_2 (not_2_out, B);
  not not_3 (not_3_out, C);
  not not_4 (not_4_out, D);
  and and_1 (and_1_out, not_2_out, D, not_3_out);
  and and_2 (and_2_out, not_2_out, C, not_4_out);
  and and_3 (and_3_out, not_1_out, B, not_4_out);
  and and_4 (and_4_out, A, not_4_out, not_2_out);
  and and_5 (and_5_out, not_1_out, B, C);
  and and_6 (and_6_out, not_1_out, not_3_out, not_4_out, B);
  and and_7 (and_7_out, A, not_3_out, D);
  and and_8 (and_8_out, not_2_out, C);
  and and_9 (and_9_out, not_1_out, B, not_3_out, not_4_out);
  and and_10 (and_10_out, A, B, not_3_out, D);
  and and_11 (and_11_out, not_1_out, not_2_out, D);
  and and_12 (and_12_out, not_1_out, C, D);
  and and_13 (and_13_out, A, not_2_out, C);
  and and_14 (and_14_out, not_2_out, not_3_out, D);
  and and_15 (and_15_out, not_1_out, B, not_4_out);
  and and_16 (and_16_out, A, not_2_out, not_4_out);
  and and_17 (and_17_out, not_1_out, B, C);
  and and_18 (and_18_out, not_1_out, C, not_4_out);
  and and_19 (and_19_out, not_1_out, B, not_4_out);
  and and_20 (and_20_out, A, not_2_out, not_3_out);
  and and_21 (and_21_out, not_1_out, D, not_2_out, not_3_out);
  and and_22 (and_22_out, A, not_2_out, not_3_out, not_4_out);
  and and_23 (and_23_out, not_1_out, C, not_4_out);
  and and_24 (and_24_out, not_1_out, B, C);
  and and_25 (and_25_out, not_1_out, B, not_4_out);
  and and_26 (and_26_out, not_2_out, not_3_out, D);
  and and_27 (and_27_out, not_2_out, C, not_4_out);
  and and_28 (and_28_out, B, not_3_out, not_4_out);
  and and_29 (and_29_out, A, not_3_out, not_4_out);
  and and_30 (and_30_out, not_1_out, B, D);
  or or_1 (or_1_out, and_1_out, and_2_out, and_5_out, and_3_out, and_4_out);
  or or_2 (or_2_out, and_6_out, and_7_out, and_8_out);
  or or_3 (or_3_out, and_9_out, and_10_out, and_11_out, and_12_out, and_13_out);
  or or_4 (or_4_out, and_14_out, and_15_out, and_16_out, and_17_out);
  or or_5 (or_5_out, and_18_out, and_19_out, and_20_out);
  or or_6 (or_6_out, and_21_out, and_22_out, and_25_out, and_23_out, and_24_out);
  or or_7 (or_7_out, and_26_out, and_27_out, and_30_out, and_28_out, and_29_out);
  _7_Segment_Display u_7_segment_display_1 (
    .g(or_7_out), .f(or_6_out), .a(or_1_out), .b(or_2_out), .e(or_5_out), .d(or_4_out), .c(or_3_out));  // open: dp
endmodule

module MUX (
  input  A,
  input  B,
  input  C,
  input  D,
  input  _1,
  input  _0
);

  wire n8_1_mux_1_f, n8_1_mux_2_f, n8_1_mux_3_f, n8_1_mux_4_f, n8_1_mux_5_f, n8_1_mux_6_f, n8_1_mux_7_f,
       not_1_out;

  not not_1 (not_1_out, D);
  _8_1_MUX u_8_1_mux_1 (
    .I0__1(D), .I1___0(not_1_out), .I2___C(not_1_out), .I3___C(_1), .I0__1_2(_1), .I1___0_2(not_1_out),
    .I2___C_2(_0), .I3___C_2(_0), .S1__A(A), .S2___B(B), .S3___C(C), .F(n8_1_mux_1_f));
  _8_1_MUX u_8_1_mux_2 (
    .I0__1(_0), .I1___0(_1), .I2___C(not_1_out), .I3___C(_0), .I0__1_2(D), .I1___0_2(_1), .I2___C_2(D),
    .I3___C_2(_0), .S1__A(A), .S2___B(B), .S3___C(C), .F(n8_1_mux_2_f));
  _8_1_MUX u_8_1_mux_3 (
    .I0__1(D), .I1___0(D), .I2___C(not_1_out), .I3___C(D), .I0__1_2(_0), .I1___0_2(_1), .I2___C_2(D),
    .I3___C_2(_0), .S1__A(A), .S2___B(B), .S3___C(C), .F(n8_1_mux_3_f));
  _8_1_MUX u_8_1_mux_4 (
    .I0__1(D), .I1___0(_0), .I2___C(not_1_out), .I3___C(_1), .I0__1_2(_1), .I1___0_2(not_1_out),
    .I2___C_2(_0), .I3___C_2(_0), .S1__A(A), .S2___B(B), .S3___C(C), .F(n8_1_mux_4_f));
  _8_1_MUX u_8_1_mux_5 (
    .I0__1(_0), .I1___0(not_1_out), .I2___C(not_1_out), .I3___C(not_1_out), .I0__1_2(_1), .I1___0_2(_0),
    .I2___C_2(_0), .I3___C_2(_0), .S1__A(A), .S2___B(B), .S3___C(C), .F(n8_1_mux_5_f));
  _8_1_MUX u_8_1_mux_6 (
    .I0__1(D), .I1___0(not_1_out), .I2___C(not_1_out), .I3___C(_1), .I0__1_2(not_1_out), .I1___0_2(_0),
    .I2___C_2(_0), .I3___C_2(_0), .S1__A(A), .S2___B(B), .S3___C(C), .F(n8_1_mux_6_f));
  _8_1_MUX u_8_1_mux_7 (
    .I0__1(D), .I1___0(not_1_out), .I2___C(_1), .I3___C(D), .I0__1_2(_1), .I1___0_2(not_1_out),
    .I2___C_2(not_1_out), .I3___C_2(_0), .S1__A(A), .S2___B(B), .S3___C(C), .F(n8_1_mux_7_f));
  _7_Segment_Display u_7_segment_display_1 (
    .g(n8_1_mux_7_f), .f(n8_1_mux_6_f), .a(n8_1_mux_1_f), .b(n8_1_mux_2_f), .e(n8_1_mux_5_f),
    .d(n8_1_mux_4_f), .c(n8_1_mux_3_f));  // open: dp
endmodule

module _8_1_MUX (
  input  I0__1,
  input  I1___0,
  input  I2___C,
  input  I3___C,
  input  I0__1_2,
  input  I1___0_2,
  input  I2___C_2,
  input  I3___C_2,
  input  S1__A,
  input  S2___B,
  input  S3___C,
  output F
);

  wire and_1_out, and_2_out, and_3_out, and_4_out, and_5_out, and_6_out, and_7_out, and_8_out, not_1_out,
       not_2_out, not_3_out, or_1_out, or_2_out, or_3_out, or_4_out, or_5_out, or_6_out;

  not not_1 (not_1_out, S1__A);
  not not_2 (not_2_out, S2___B);
  not not_3 (not_3_out, S3___C);
  and and_1 (and_1_out, I0__1, not_2_out, not_1_out, not_3_out);
  and and_2 (and_2_out, I1___0, not_2_out, not_1_out, S3___C);
  and and_3 (and_3_out, I2___C, S2___B, not_1_out, not_3_out);
  and and_4 (and_4_out, I3___C, S2___B, not_1_out, S3___C);
  and and_5 (and_5_out, I0__1_2, not_2_out, S1__A, not_3_out);
  and and_6 (and_6_out, I1___0_2, not_2_out, S1__A, S3___C);
  and and_7 (and_7_out, I2___C_2, S2___B, S1__A, not_3_out);
  and and_8 (and_8_out, I3___C_2, S2___B, S1__A, S3___C);
  or or_1 (or_1_out, and_1_out, and_2_out);
  or or_2 (or_2_out, and_3_out, and_4_out);
  or or_3 (or_3_out, and_5_out, and_6_out);
  or or_4 (or_4_out, and_7_out, and_8_out);
  or or_5 (or_5_out, or_1_out, or_2_out);
  or or_6 (or_6_out, or_3_out, or_4_out);
  or or_7 (F, or_5_out, or_6_out);
endmodule

module Sequential_D_Flip_Flop (
  input  in_1
);

  wire and_1_out, and_2_out, and_3_out, and_4_out, and_5_out, and_6_out, and_7_out, and_8_out, and_9_out,
       and_10_out, and_11_out, and_12_out, and_13_out, and_14_out, and_15_out, clock_1_out, d_ff_1_q,
       d_ff_1_qn, d_ff_2_q, d_ff_2_qn, d_ff_3_q, d_ff_4_q, d_ff_4_qn, not_1_out, or_1_out, or_2_out, or_3_out;

  not not_1 (not_1_out, in_1);
  and and_1 (and_1_out, not_1_out, d_ff_1_qn, d_ff_2_qn, d_ff_2_qn, d_ff_4_qn);
  and and_2 (and_2_out, in_1, d_ff_1_qn, d_ff_2_q, d_ff_3_q, d_ff_4_q);
  and and_3 (and_3_out, d_ff_1_q, d_ff_2_qn, d_ff_4_q);
  and and_4 (and_4_out, d_ff_1_q, d_ff_2_qn, d_ff_3_q);
  and and_5 (and_5_out, not_1_out, d_ff_1_q, d_ff_2_q);
  and and_6 (and_6_out, in_1, d_ff_1_q, d_ff_4_qn);
  and and_7 (and_7_out, not_1_out, d_ff_2_qn, d_ff_2_qn, d_ff_4_qn);
  and and_8 (and_8_out, in_1, d_ff_2_qn, d_ff_3_q, d_ff_4_q);
  and and_9 (and_9_out, not_1_out, d_ff_2_q, d_ff_3_q);
  and and_10 (and_10_out, d_ff_2_q, d_ff_2_qn, d_ff_4_q);
  and and_11 (and_11_out, in_1, d_ff_2_q, d_ff_4_qn);
  and and_12 (and_12_out, not_1_out, d_ff_2_qn, d_ff_4_qn);
  and and_13 (and_13_out, not_1_out, d_ff_3_q, d_ff_4_q);
  and and_14 (and_14_out, in_1, d_ff_2_qn, d_ff_4_qn);
  and and_15 (and_15_out, in_1, d_ff_3_q, d_ff_4_qn);
  or or_1 (or_1_out, and_1_out, and_2_out, and_3_out, and_4_out, and_5_out, and_6_out);
  or or_2 (or_2_out, and_7_out, and_8_out, and_9_out, and_10_out, and_11_out);
  or or_3 (or_3_out, and_12_out, and_13_out, and_14_out, and_15_out);
  Clock clock_1 (.out(clock_1_out));
  D_Flip_Flop d_ff_1 (.clk(clock_1_out), .D(or_1_out), .Q(d_ff_1_q), .Qn(d_ff_1_qn));  // open: preset, en, reset
  D_Flip_Flop d_ff_2 (.clk(clock_1_out), .D(or_2_out), .Q(d_ff_2_q), .Qn(d_ff_2_qn));  // open: preset, en, reset
  D_Flip_Flop d_ff_3 (.clk(clock_1_out), .D(or_3_out), .Q(d_ff_3_q), .Qn(d_ff_2_qn));  // open: preset, en, reset
  D_Flip_Flop d_ff_4 (.clk(clock_1_out), .D(d_ff_4_qn), .Q(d_ff_4_q), .Qn(d_ff_4_qn));  // open: preset, en, reset
endmodule

module Sequential_Test (
  input  in_1,
  input  A,
  input  B,
  input  C,
  input  D,
  input  in_6,
  input  _1,
  input  _0
);

  wire and_1_out, and_2_out, and_3_out, and_4_out, and_5_out, and_6_out, and_7_out, and_8_out, and_9_out,
       and_10_out, clock_1_out, d_ff_1_q, d_ff_1_qn, n8_1_mux_1_f, n8_1_mux_2_f, n8_1_mux_3_f, n8_1_mux_4_f,
       n8_1_mux_5_f, n8_1_mux_6_f, n8_1_mux_7_f, not_1_out, not_2_out, or_1_out, or_2_out, or_3_out,
       or_4_out, t_ff_1_q, t_ff_1_qn, t_ff_2_q, t_ff_2_qn, t_ff_3_q, t_ff_3_qn;

  not not_1 (not_1_out, in_1);
  and and_1 (and_1_out, t_ff_1_qn, t_ff_2_qn, t_ff_3_qn, not_1_out);
  and and_2 (and_2_out, t_ff_2_qn, t_ff_3_qn, d_ff_1_qn, not_1_out);
  and and_3 (and_3_out, t_ff_2_q, t_ff_3_q, d_ff_1_q, in_1);
  and and_4 (and_4_out, t_ff_1_q, t_ff_2_q, d_ff_1_q, in_1);
  and and_5 (and_5_out, t_ff_3_qn, d_ff_1_qn, not_1_out);
  and and_6 (and_6_out, t_ff_3_q, d_ff_1_q, in_1);
  and and_7 (and_7_out, t_ff_1_qn, d_ff_1_q, in_1);
  and and_8 (and_8_out, t_ff_2_qn, d_ff_1_q, in_1);
  and and_9 (and_9_out, d_ff_1_qn, not_1_out);
  and and_10 (and_10_out, t_ff_1_q, t_ff_2_q, in_1);
  or or_1 (or_1_out, and_1_out, and_2_out, and_3_out, and_4_out);
  or or_2 (or_2_out, and_1_out, and_4_out, and_5_out, and_6_out);
  or or_3 (or_3_out, and_7_out, and_8_out, and_9_out);
  or or_4 (or_4_out, and_1_out, and_10_out, d_ff_1_qn);
  T_Flip_Flop t_ff_1 (.clk(clock_1_out), .T(or_1_out), .Q(t_ff_1_q), .Qn(t_ff_1_qn), .reset(in_6));  // open: preset, en
  T_Flip_Flop t_ff_2 (.clk(clock_1_out), .T(or_2_out), .Q(t_ff_2_q), .Qn(t_ff_2_qn), .reset(in_6));  // open: preset, en
  T_Flip_Flop t_ff_3 (.clk(clock_1_out), .T(or_3_out), .Q(t_ff_3_q), .Qn(t_ff_3_qn), .reset(in_6));  // open: preset, en
  D_Flip_Flop d_ff_1 (.clk(clock_1_out), .D(or_4_out), .Q(d_ff_1_q), .Qn(d_ff_1_qn), .reset(in_6));  // open: preset, en
  not not_2 (not_2_out, d_ff_1_q);
  _8_1_MUX u_8_1_mux_1 (
    .I0__1(d_ff_1_q), .I1___0(not_2_out), .I2___C(not_2_out), .I3___C(_1), .I0__1_2(_1),
    .I1___0_2(not_2_out), .I2___C_2(_0), .I3___C_2(_0), .S1__A(t_ff_1_q), .S2___B(t_ff_2_q),
    .S3___C(t_ff_3_q), .F(n8_1_mux_1_f));
  _8_1_MUX u_8_1_mux_2 (
    .I0__1(_0), .I1___0(_1), .I2___C(not_2_out), .I3___C(_0), .I0__1_2(d_ff_1_q), .I1___0_2(_1),
    .I2___C_2(d_ff_1_q), .I3___C_2(_0), .S1__A(t_ff_1_q), .S2___B(t_ff_2_q), .S3___C(t_ff_3_q),
    .F(n8_1_mux_2_f));
  _8_1_MUX u_8_1_mux_3 (
    .I0__1(d_ff_1_q), .I1___0(d_ff_1_q), .I2___C(not_2_out), .I3___C(d_ff_1_q), .I0__1_2(_0), .I1___0_2(_1),
    .I2___C_2(d_ff_1_q), .I3___C_2(_0), .S1__A(t_ff_1_q), .S2___B(t_ff_2_q), .S3___C(t_ff_3_q),
    .F(n8_1_mux_3_f));
  _8_1_MUX u_8_1_mux_4 (
    .I0__1(d_ff_1_q), .I1___0(_0), .I2___C(not_2_out), .I3___C(_1), .I0__1_2(_1), .I1___0_2(not_2_out),
    .I2___C_2(_0), .I3___C_2(_0), .S1__A(t_ff_1_q), .S2___B(t_ff_2_q), .S3___C(t_ff_3_q), .F(n8_1_mux_4_f));
  _8_1_MUX u_8_1_mux_5 (
    .I0__1(_0), .I1___0(not_2_out), .I2___C(not_2_out), .I3___C(not_2_out), .I0__1_2(_1), .I1___0_2(_0),
    .I2___C_2(_0), .I3___C_2(_0), .S1__A(t_ff_1_q), .S2___B(t_ff_2_q), .S3___C(t_ff_3_q), .F(n8_1_mux_5_f));
  _8_1_MUX u_8_1_mux_6 (
    .I0__1(d_ff_1_q), .I1___0(not_2_out), .I2___C(not_2_out), .I3___C(_1), .I0__1_2(not_2_out),
    .I1___0_2(_0), .I2___C_2(_0), .I3___C_2(_0), .S1__A(t_ff_1_q), .S2___B(t_ff_2_q), .S3___C(t_ff_3_q),
    .F(n8_1_mux_6_f));
  _8_1_MUX u_8_1_mux_7 (
    .I0__1(d_ff_1_q), .I1___0(not_2_out), .I2___C(_1), .I3___C(d_ff_1_q), .I0__1_2(_1), .I1___0_2(not_2_out),
    .I2___C_2(not_2_out), .I3___C_2(_0), .S1__A(t_ff_1_q), .S2___B(t_ff_2_q), .S3___C(t_ff_3_q),
    .F(n8_1_mux_7_f));
  Clock clock_1 (.out(clock_1_out));
  _7_Segment_Display u_7_segment_display_1 (
    .g(n8_1_mux_7_f), .f(n8_1_mux_6_f), .a(n8_1_mux_1_f), .b(n8_1_mux_2_f), .e(n8_1_mux_5_f),
    .d(n8_1_mux_4_f), .c(n8_1_mux_3_f));  // open: dp
endmodule

module NEW_CIRCUIT (
  input  in_1,
  input  in_2,
  input  _1,
  input  _0
);

  wire and_1_out, and_2_out, and_3_out, and_4_out, and_5_out, and_6_out, and_7_out, and_8_out, and_9_out,
       and_10_out, clock_1_out, d_ff_1_q, d_ff_1_qn, n8_1_mux_1_f, n8_1_mux_2_f, n8_1_mux_3_f, n8_1_mux_4_f,
       n8_1_mux_5_f, n8_1_mux_6_f, n8_1_mux_7_f, not_1_out, not_2_out, or_1_out, or_2_out, or_3_out,
       or_4_out, t_ff_1_q, t_ff_1_qn, t_ff_2_q, t_ff_2_qn, t_ff_3_q, t_ff_3_qn;

  T_Flip_Flop t_ff_1 (.clk(clock_1_out), .T(or_1_out), .Q(t_ff_1_q), .Qn(t_ff_1_qn), .reset(in_2));  // open: preset, en
  T_Flip_Flop t_ff_2 (.clk(clock_1_out), .T(or_2_out), .Q(t_ff_2_q), .Qn(t_ff_2_qn), .reset(in_2));  // open: preset, en
  T_Flip_Flop t_ff_3 (.clk(clock_1_out), .T(or_3_out), .Q(t_ff_3_q), .Qn(t_ff_3_qn), .reset(in_2));  // open: preset, en
  D_Flip_Flop d_ff_1 (.clk(clock_1_out), .D(or_4_out), .Q(d_ff_1_q), .Qn(d_ff_1_qn), .reset(in_2));  // open: preset, en
  not not_1 (not_1_out, in_1);
  and and_1 (and_1_out, t_ff_1_qn, t_ff_2_qn, t_ff_3_qn, not_1_out);
  and and_2 (and_2_out, t_ff_2_qn, t_ff_3_qn, d_ff_1_qn, not_1_out);
  and and_3 (and_3_out, t_ff_1_q, t_ff_2_q, d_ff_1_q, in_1);
  and and_4 (and_4_out, t_ff_2_q, t_ff_3_q, d_ff_1_q, in_1);
  and and_5 (and_5_out, t_ff_3_qn, d_ff_1_qn, not_1_out);
  and and_6 (and_6_out, t_ff_3_q, d_ff_1_q, in_1);
  and and_7 (and_7_out, t_ff_1_qn, d_ff_1_q, in_1);
  and and_8 (and_8_out, t_ff_2_qn, d_ff_1_q, in_1);
  and and_9 (and_9_out, d_ff_1_qn, not_1_out);
  and and_10 (and_10_out, t_ff_1_q, t_ff_2_q, in_1);
  or or_1 (or_1_out, and_1_out, and_2_out, and_3_out, and_4_out);
  or or_2 (or_2_out, and_5_out, and_6_out, and_1_out, and_3_out);
  or or_3 (or_3_out, and_7_out, and_8_out, and_9_out);
  or or_4 (or_4_out, and_1_out, and_10_out, d_ff_1_qn);
  not not_2 (not_2_out, d_ff_1_q);
  Clock clock_1 (.out(clock_1_out));
  _8_1_MUX u_8_1_mux_1 (
    .I0__1(d_ff_1_q), .I1___0(not_2_out), .I2___C(not_2_out), .I3___C(_1), .I0__1_2(_1),
    .I1___0_2(not_2_out), .I2___C_2(_0), .I3___C_2(_0), .S1__A(t_ff_1_q), .S2___B(t_ff_2_q),
    .S3___C(t_ff_3_q), .F(n8_1_mux_1_f));
  _8_1_MUX u_8_1_mux_2 (
    .I0__1(_0), .I1___0(_1), .I2___C(not_2_out), .I3___C(_0), .I0__1_2(d_ff_1_q), .I1___0_2(_1),
    .I2___C_2(d_ff_1_q), .I3___C_2(_0), .S1__A(t_ff_1_q), .S2___B(t_ff_2_q), .S3___C(t_ff_3_q),
    .F(n8_1_mux_2_f));
  _8_1_MUX u_8_1_mux_3 (
    .I0__1(d_ff_1_q), .I1___0(d_ff_1_q), .I2___C(not_2_out), .I3___C(d_ff_1_q), .I0__1_2(_0), .I1___0_2(_1),
    .I2___C_2(d_ff_1_q), .I3___C_2(_0), .S1__A(t_ff_1_q), .S2___B(t_ff_2_q), .S3___C(t_ff_3_q),
    .F(n8_1_mux_3_f));
  _8_1_MUX u_8_1_mux_4 (
    .I0__1(d_ff_1_q), .I1___0(_0), .I2___C(not_2_out), .I3___C(_1), .I0__1_2(_1), .I1___0_2(not_2_out),
    .I2___C_2(_0), .I3___C_2(_0), .S1__A(t_ff_1_q), .S2___B(t_ff_2_q), .S3___C(t_ff_3_q), .F(n8_1_mux_4_f));
  _8_1_MUX u_8_1_mux_5 (
    .I0__1(_0), .I1___0(not_2_out), .I2___C(not_2_out), .I3___C(not_2_out), .I0__1_2(_1), .I1___0_2(_0),
    .I2___C_2(_0), .I3___C_2(_0), .S1__A(t_ff_1_q), .S2___B(t_ff_2_q), .S3___C(t_ff_3_q), .F(n8_1_mux_5_f));
  _8_1_MUX u_8_1_mux_6 (
    .I0__1(d_ff_1_q), .I1___0(not_2_out), .I2___C(not_2_out), .I3___C(_1), .I0__1_2(not_2_out),
    .I1___0_2(_0), .I2___C_2(_0), .I3___C_2(_0), .S1__A(t_ff_1_q), .S2___B(t_ff_2_q), .S3___C(t_ff_3_q),
    .F(n8_1_mux_6_f));
  _8_1_MUX u_8_1_mux_7 (
    .I0__1(d_ff_1_q), .I1___0(not_2_out), .I2___C(_1), .I3___C(d_ff_1_q), .I0__1_2(_1), .I1___0_2(not_2_out),
    .I2___C_2(not_2_out), .I3___C_2(_0), .S1__A(t_ff_1_q), .S2___B(t_ff_2_q), .S3___C(t_ff_3_q),
    .F(n8_1_mux_7_f));
  _7_Segment_Display u_7_segment_display_1 (
    .g(n8_1_mux_7_f), .f(n8_1_mux_6_f), .a(n8_1_mux_1_f), .b(n8_1_mux_2_f), .e(n8_1_mux_5_f),
    .d(n8_1_mux_4_f), .c(n8_1_mux_3_f));  // open: dp
endmodule
